# Fritzing sketch button_motor (saved by Fritzing 0.9.3b)
breadboards: 1

parts:
  Part1 = EasyDriver_v44
  M1 = Stepper Motor - Bipolar
  Part2 = Arduino Uno (Rev3) - ICSP
  S1 = Pushbutton [package="[THT]"]
  Power_plug1 = Power plug  # not connected

nets:
  GND: Part1.GND, Part2.GND, S1.Pin_3, S1.Pin_4
  N1: Part1.V+, Part2.VIN
  N2: Part1.STEP, Part2.D9_PWM
  N3: Part1.DIR, Part2.D8
  N4: Part1.OUT2A, M1.A
  N5: Part1.OUT2B, M1.C
  N6: Part1.OUT1A, M1.B
  N7: Part1.OUT1B, M1.D
  N8: Part2.D4, S1.Pin_1, S1.Pin_2
