# Fritzing sketch two_motors (saved by Fritzing 0.9.3b)
breadboards: 1

parts:
  Part4 = EasyDriver_v44
  M2 = Stepper Motor - Bipolar
  Part3 = Arduino Uno (Rev3) - ICSP
  M3 = Stepper Motor - Bipolar
  Part5 = EasyDriver_v44
  Power_plug1 = Power plug  # not connected

nets:
  GND: Part4.GND, Part3.GND, Part5.GND
  N1: Part4.V+, Part3.VIN, Part5.V+
  N2: Part4.STEP, Part3.D7
  N3: Part4.DIR, Part3.D6_PWM
  N4: Part4.OUT2A, M2.A
  N5: Part4.OUT2B, M2.C
  N6: Part4.OUT1A, M2.B
  N7: Part4.OUT1B, M2.D
  N8: Part3.D8, Part5.DIR
  N9: Part3.D9_PWM, Part5.STEP
  N10: M3.A, Part5.OUT2A
  N11: M3.C, Part5.OUT2B
  N12: M3.B, Part5.OUT1A
  N13: M3.D, Part5.OUT1B

notes:
  motor UP/DOWN
  motor LEFT/RIGHT
